// Logisim project Proj2.circ as structural Verilog: 4 circuits, main circuit regfile
module CPUmain (
  input  [31:0] in_1
);

  wire control_1_imm_sel, control_1_reg_write_e;
  wire [3:0] control_1_alu_code;
  wire [4:0] control_1_rd, control_1_rs, control_1_rt;
  wire [15:0] control_1_imm;
  wire [31:0] alu_1_res, bit_extender_1_out, multiplexer_1_out, regfile_1_rs_data, regfile_1_rt_data;

  regfile regfile_1 (
    .rt(control_1_rt), .rd(control_1_rd), .rd_data(alu_1_res), .write_e(control_1_reg_write_e),
    .rs(control_1_rs), .rs_data(regfile_1_rs_data), .rt_data(regfile_1_rt_data));
  Control control_1 (
    .Inst(in_1), .rs(control_1_rs), .rt(control_1_rt), .rd(control_1_rd), .imm(control_1_imm),
    .reg_write_e(control_1_reg_write_e), .imm_sel(control_1_imm_sel), .ALU_code(control_1_alu_code));
  assign bit_extender_1_out = {{16{control_1_imm[15]}}, control_1_imm};  // Bit_Extender bit_extender_1
  Multiplexer #(.width(32)) multiplexer_1 (
    .in0(regfile_1_rt_data), .in1(bit_extender_1_out), .out(multiplexer_1_out), .sel(control_1_imm_sel));
  ALU alu_1 (.OP1(regfile_1_rs_data), .OP2(multiplexer_1_out), .ALU_CODE(control_1_alu_code), .Res(alu_1_res));
endmodule

module regfile (
  input  [4:0] rs,
  input  [4:0] rt,
  input  [4:0] rd,
  input  write_e,
  input  [31:0] rd_data,
  output [31:0] rs_data,
  output [31:0] rt_data
);

  wire clock_1_out, demultiplexer_2_out1, demultiplexer_2_out2, demultiplexer_2_out3, demultiplexer_2_out4,
       demultiplexer_2_out5, demultiplexer_2_out6, demultiplexer_2_out7, demultiplexer_2_out8,
       demultiplexer_2_out9, demultiplexer_2_out10, demultiplexer_2_out11, demultiplexer_2_out12,
       demultiplexer_2_out13, demultiplexer_2_out14, demultiplexer_2_out15, demultiplexer_2_out16,
       demultiplexer_2_out17, demultiplexer_2_out18, demultiplexer_2_out19, demultiplexer_2_out20,
       demultiplexer_2_out21, demultiplexer_2_out22, demultiplexer_2_out23, demultiplexer_2_out24,
       demultiplexer_2_out25, demultiplexer_2_out26, demultiplexer_2_out27, demultiplexer_2_out28,
       demultiplexer_2_out29, demultiplexer_2_out30, demultiplexer_2_out31;
  wire [31:0] a0_q, a1_q, a2_q, a3_q, at_q, demultiplexer_1_out0, demultiplexer_1_out1, demultiplexer_1_out2,
       demultiplexer_1_out3, demultiplexer_1_out4, demultiplexer_1_out5, demultiplexer_1_out6,
       demultiplexer_1_out7, demultiplexer_1_out8, demultiplexer_1_out9, demultiplexer_1_out10,
       demultiplexer_1_out11, demultiplexer_1_out12, demultiplexer_1_out13, demultiplexer_1_out14,
       demultiplexer_1_out15, demultiplexer_1_out16, demultiplexer_1_out17, demultiplexer_1_out18,
       demultiplexer_1_out19, demultiplexer_1_out20, demultiplexer_1_out21, demultiplexer_1_out22,
       demultiplexer_1_out23, demultiplexer_1_out24, demultiplexer_1_out25, demultiplexer_1_out26,
       demultiplexer_1_out27, demultiplexer_1_out28, demultiplexer_1_out29, demultiplexer_1_out30,
       demultiplexer_1_out31, fp_q, gp_q, k0_q, k1_q, ra_q, s0_q, s1_q, s2_q, s3_q, s4_q, s5_q, s6_q, s7_q,
       sp_q, t0_q, t1_q, t2_q, t3_q, t4_q, t5_q, t6_q, t7_q, t8_q, t9_q, v0_q, v1_q, zero_q;

  Demultiplexer #(.select(5), .width(32)) demultiplexer_1 (
    .out0(demultiplexer_1_out0), .out1(demultiplexer_1_out1), .out2(demultiplexer_1_out2),
    .out3(demultiplexer_1_out3), .out4(demultiplexer_1_out4), .out5(demultiplexer_1_out5),
    .out6(demultiplexer_1_out6), .out7(demultiplexer_1_out7), .out8(demultiplexer_1_out8),
    .out9(demultiplexer_1_out9), .out10(demultiplexer_1_out10), .out11(demultiplexer_1_out11),
    .out12(demultiplexer_1_out12), .out13(demultiplexer_1_out13), .out14(demultiplexer_1_out14),
    .out15(demultiplexer_1_out15), .out16(demultiplexer_1_out16), .out17(demultiplexer_1_out17),
    .out18(demultiplexer_1_out18), .out19(demultiplexer_1_out19), .out20(demultiplexer_1_out20),
    .out21(demultiplexer_1_out21), .out22(demultiplexer_1_out22), .out23(demultiplexer_1_out23),
    .out24(demultiplexer_1_out24), .out25(demultiplexer_1_out25), .out26(demultiplexer_1_out26),
    .out27(demultiplexer_1_out27), .out28(demultiplexer_1_out28), .out29(demultiplexer_1_out29),
    .out30(demultiplexer_1_out30), .out31(demultiplexer_1_out31), .in(rd_data), .sel(rd));
  Demultiplexer #(.select(5)) demultiplexer_2 (
    .out1(demultiplexer_2_out1), .out2(demultiplexer_2_out2), .out3(demultiplexer_2_out3),
    .out4(demultiplexer_2_out4), .out5(demultiplexer_2_out5), .out6(demultiplexer_2_out6),
    .out7(demultiplexer_2_out7), .out8(demultiplexer_2_out8), .out9(demultiplexer_2_out9),
    .out10(demultiplexer_2_out10), .out11(demultiplexer_2_out11), .out12(demultiplexer_2_out12),
    .out13(demultiplexer_2_out13), .out14(demultiplexer_2_out14), .out15(demultiplexer_2_out15),
    .out16(demultiplexer_2_out16), .out17(demultiplexer_2_out17), .out18(demultiplexer_2_out18),
    .out19(demultiplexer_2_out19), .out20(demultiplexer_2_out20), .out21(demultiplexer_2_out21),
    .out22(demultiplexer_2_out22), .out23(demultiplexer_2_out23), .out24(demultiplexer_2_out24),
    .out25(demultiplexer_2_out25), .out26(demultiplexer_2_out26), .out27(demultiplexer_2_out27),
    .out28(demultiplexer_2_out28), .out29(demultiplexer_2_out29), .out30(demultiplexer_2_out30),
    .out31(demultiplexer_2_out31), .in(write_e), .sel(rd));  // open: out0
  Clock clock_1 (.out(clock_1_out));
  Register #(.width(32)) zero (.D(demultiplexer_1_out0), .en(1'b0), .clk(clock_1_out), .Q(zero_q));  // open: clr
  Register #(.width(32)) at (
    .D(demultiplexer_1_out1), .en(demultiplexer_2_out1), .clk(clock_1_out), .Q(at_q));  // open: clr
  Register #(.width(32)) v0 (
    .D(demultiplexer_1_out2), .en(demultiplexer_2_out2), .clk(clock_1_out), .Q(v0_q));  // open: clr
  Register #(.width(32)) v1 (
    .D(demultiplexer_1_out3), .en(demultiplexer_2_out3), .clk(clock_1_out), .Q(v1_q));  // open: clr
  Register #(.width(32)) a0 (
    .D(demultiplexer_1_out4), .en(demultiplexer_2_out4), .clk(clock_1_out), .Q(a0_q));  // open: clr
  Register #(.width(32)) a1 (
    .D(demultiplexer_1_out5), .en(demultiplexer_2_out5), .clk(clock_1_out), .Q(a1_q));  // open: clr
  Register #(.width(32)) a2 (
    .D(demultiplexer_1_out6), .en(demultiplexer_2_out6), .clk(clock_1_out), .Q(a2_q));  // open: clr
  Register #(.width(32)) a3 (
    .D(demultiplexer_1_out7), .en(demultiplexer_2_out7), .clk(clock_1_out), .Q(a3_q));  // open: clr
  Register #(.width(32)) t0 (
    .D(demultiplexer_1_out8), .en(demultiplexer_2_out8), .clk(clock_1_out), .Q(t0_q));  // open: clr
  Register #(.width(32)) t1 (
    .D(demultiplexer_1_out9), .en(demultiplexer_2_out9), .clk(clock_1_out), .Q(t1_q));  // open: clr
  Register #(.width(32)) t2 (
    .D(demultiplexer_1_out10), .en(demultiplexer_2_out10), .clk(clock_1_out), .Q(t2_q));  // open: clr
  Register #(.width(32)) t3 (
    .D(demultiplexer_1_out11), .en(demultiplexer_2_out11), .clk(clock_1_out), .Q(t3_q));  // open: clr
  Register #(.width(32)) t4 (
    .D(demultiplexer_1_out12), .en(demultiplexer_2_out12), .clk(clock_1_out), .Q(t4_q));  // open: clr
  Register #(.width(32)) t5 (
    .D(demultiplexer_1_out13), .en(demultiplexer_2_out13), .clk(clock_1_out), .Q(t5_q));  // open: clr
  Register #(.width(32)) t6 (
    .D(demultiplexer_1_out14), .en(demultiplexer_2_out14), .clk(clock_1_out), .Q(t6_q));  // open: clr
  Register #(.width(32)) t7 (
    .D(demultiplexer_1_out15), .en(demultiplexer_2_out15), .clk(clock_1_out), .Q(t7_q));  // open: clr
  Register #(.width(32)) s0 (
    .D(demultiplexer_1_out16), .en(demultiplexer_2_out16), .clk(clock_1_out), .Q(s0_q));  // open: clr
  Register #(.width(32)) s1 (
    .D(demultiplexer_1_out17), .en(demultiplexer_2_out17), .clk(clock_1_out), .Q(s1_q));  // open: clr
  Register #(.width(32)) s2 (
    .D(demultiplexer_1_out18), .en(demultiplexer_2_out18), .clk(clock_1_out), .Q(s2_q));  // open: clr
  Register #(.width(32)) s3 (
    .D(demultiplexer_1_out19), .en(demultiplexer_2_out19), .clk(clock_1_out), .Q(s3_q));  // open: clr
  Register #(.width(32)) s4 (
    .D(demultiplexer_1_out20), .en(demultiplexer_2_out20), .clk(clock_1_out), .Q(s4_q));  // open: clr
  Register #(.width(32)) s5 (
    .D(demultiplexer_1_out21), .en(demultiplexer_2_out21), .clk(clock_1_out), .Q(s5_q));  // open: clr
  Register #(.width(32)) s6 (
    .D(demultiplexer_1_out22), .en(demultiplexer_2_out22), .clk(clock_1_out), .Q(s6_q));  // open: clr
  Register #(.width(32)) s7 (
    .D(demultiplexer_1_out23), .en(demultiplexer_2_out23), .clk(clock_1_out), .Q(s7_q));  // open: clr
  Register #(.width(32)) t8 (
    .D(demultiplexer_1_out24), .en(demultiplexer_2_out24), .clk(clock_1_out), .Q(t8_q));  // open: clr
  Register #(.width(32)) t9 (
    .D(demultiplexer_1_out25), .en(demultiplexer_2_out25), .clk(clock_1_out), .Q(t9_q));  // open: clr
  Register #(.width(32)) k0 (
    .D(demultiplexer_1_out26), .en(demultiplexer_2_out26), .clk(clock_1_out), .Q(k0_q));  // open: clr
  Register #(.width(32)) k1 (
    .D(demultiplexer_1_out27), .en(demultiplexer_2_out27), .clk(clock_1_out), .Q(k1_q));  // open: clr
  Register #(.width(32)) gp (
    .D(demultiplexer_1_out28), .en(demultiplexer_2_out28), .clk(clock_1_out), .Q(gp_q));  // open: clr
  Register #(.width(32)) sp (
    .D(demultiplexer_1_out29), .en(demultiplexer_2_out29), .clk(clock_1_out), .Q(sp_q));  // open: clr
  Register #(.width(32)) fp (
    .D(demultiplexer_1_out30), .en(demultiplexer_2_out30), .clk(clock_1_out), .Q(fp_q));  // open: clr
  Register #(.width(32)) ra (
    .D(demultiplexer_1_out31), .en(demultiplexer_2_out31), .clk(clock_1_out), .Q(ra_q));  // open: clr
  Multiplexer #(.select(5), .width(32)) multiplexer_1 (
    .in0(zero_q), .in1(at_q), .in2(v0_q), .in3(v1_q), .in4(a0_q), .in5(a1_q), .in6(a2_q), .in7(a3_q),
    .in8(t0_q), .in9(t1_q), .in10(t2_q), .in11(t3_q), .in12(t4_q), .in13(t5_q), .in14(t6_q), .in15(t7_q),
    .in16(s0_q), .in17(s1_q), .in18(s2_q), .in19(s3_q), .in20(s4_q), .in21(s5_q), .in22(s6_q), .in23(s7_q),
    .in24(t8_q), .in25(t9_q), .in26(k0_q), .in27(k1_q), .in28(gp_q), .in29(sp_q), .in30(fp_q), .in31(ra_q),
    .out(rs_data), .sel(rs));
  Multiplexer #(.select(5), .width(32)) multiplexer_2 (
    .in0(zero_q), .in1(at_q), .in2(v0_q), .in3(v1_q), .in4(a0_q), .in5(a1_q), .in6(a2_q), .in7(a3_q),
    .in8(t0_q), .in9(t1_q), .in10(t2_q), .in11(t3_q), .in12(t4_q), .in13(t5_q), .in14(t6_q), .in15(t7_q),
    .in16(s0_q), .in17(s1_q), .in18(s2_q), .in19(s3_q), .in20(s4_q), .in21(s5_q), .in22(s6_q), .in23(s7_q),
    .in24(t8_q), .in25(t9_q), .in26(k0_q), .in27(k1_q), .in28(gp_q), .in29(sp_q), .in30(fp_q), .in31(ra_q),
    .out(rt_data), .sel(rt));
endmodule

module ALU (
  input  [3:0] ALU_CODE,
  input  [31:0] OP1,
  input  [31:0] OP2,
  output [31:0] Res
);

  wire clock_1_out, comparator_1_lt, comparator_2_eq, comparator_3_eq, or_2_out;
  wire [4:0] bit_extender_2_out, bit_extender_3_out;
  wire [15:0] bit_extender_1_out;
  wire [31:0] adder_1_out, and_1_out, bit_extender_4_out, divider_1_out, divider_1_rem, HI_q, LO_q,
       multiplexer_1_out, multiplexer_2_out, multiplier_1_cout, multiplier_1_out, nor_1_out, or_1_out,
       shifter_1_out, shifter_2_out, subtractor_1_out, xor_1_out;

  Bit_Extender #(.in_width(32)) bit_extender_1 (.in(OP2), .out(bit_extender_1_out));
  Adder #(.width(32)) adder_1 (.a(OP1), .b(OP2), .out(adder_1_out));  // open: cin, cout
  Subtractor #(.width(32)) subtractor_1 (.a(OP1), .b(OP2), .out(subtractor_1_out));  // open: bin, bout
  Multiplier #(.width(32)) multiplier_1 (
    .a(OP1), .b(OP2), .out(multiplier_1_out), .cout(multiplier_1_cout));  // open: cin
  Divider #(.width(32)) divider_1 (.a(OP1), .b(OP2), .out(divider_1_out), .rem(divider_1_rem));  // open: upper
  Bit_Extender #(.in_width(32), .out_width(5)) bit_extender_2 (.in(OP2), .out(bit_extender_2_out));
  Bit_Extender #(.in_width(32), .out_width(5)) bit_extender_3 (.in(OP2), .out(bit_extender_3_out));
  Comparator #(.width(32)) comparator_1 (.a(OP1), .b(OP2), .lt(comparator_1_lt));  // open: gt, eq
  assign and_1_out = OP1 & OP2;  // AND_Gate and_1, 32 bits wide
  assign or_1_out = OP1 | OP2;  // OR_Gate or_1, 32 bits wide
  assign nor_1_out = ~(OP1 | OP2);  // NOR_Gate nor_1, 32 bits wide
  assign xor_1_out = OP1 ^ OP2;  // XOR_Gate xor_1, 32 bits wide
  Shifter #(.width(32)) shifter_1 (.in(OP1), .\dist (bit_extender_2_out), .out(shifter_1_out));
  Shifter #(.shift("lr"), .width(32)) shifter_2 (.in(OP1), .\dist (bit_extender_3_out), .out(shifter_2_out));
  assign bit_extender_4_out = {{31{1'b0}}, comparator_1_lt};  // Bit_Extender bit_extender_4
  Comparator #(.width(4)) comparator_2 (.a(4'b0010), .b(ALU_CODE), .eq(comparator_2_eq));  // open: gt, lt
  Comparator #(.width(4)) comparator_3 (.a(4'b0011), .b(ALU_CODE), .eq(comparator_3_eq));  // open: gt, lt
  Multiplexer #(.width(32)) multiplexer_1 (
    .in0(divider_1_rem), .in1(multiplier_1_cout), .out(multiplexer_1_out), .sel(comparator_2_eq));
  or or_2 (or_2_out, comparator_2_eq, comparator_3_eq);
  Multiplexer #(.width(32)) multiplexer_2 (
    .in0(multiplier_1_out), .in1(divider_1_out), .out(multiplexer_2_out), .sel(comparator_3_eq));
  // Probe on multiplexer_1_out
  // Probe on multiplexer_2_out
  Register #(.width(32)) HI (.D(multiplexer_1_out), .en(or_2_out), .clk(clock_1_out), .Q(HI_q));  // open: clr
  Clock clock_1 (.out(clock_1_out));
  Register #(.width(32)) LO (.D(multiplexer_2_out), .en(or_2_out), .clk(clock_1_out), .Q(LO_q));  // open: clr
  Multiplexer #(.select(4), .width(32)) multiplexer_3 (
    .in0(adder_1_out), .in1(subtractor_1_out), .in4(LO_q), .in5(HI_q), .in6(shifter_1_out),
    .in7(shifter_2_out), .in8(bit_extender_4_out), .in9(and_1_out), .in10(or_1_out), .in11(nor_1_out),
    .in12(xor_1_out), .in13({bit_extender_1_out, {16{1'b0}}}), .out(Res), .sel(ALU_CODE));  // open: in2, in3, in14, in15

  // Notes on the sheet:
  //   and & andi 
  //   or & ori
  //   nor
  //   xor & xori
  //   LUI
  //   shamt
  //   shamt
  //   slt
  //   sll
  //   srl
endmodule

module Control (
  input  [31:0] Inst,
  output [4:0] rs,
  output [4:0] rt,
  output [4:0] rd,
  output [15:0] imm,
  output reg_write_e,
  output imm_sel,
  output [3:0] ALU_code
);

  wire and_1_out, and_2_out, and_3_out, and_4_out, and_5_out, and_6_out, and_7_out, and_8_out, and_9_out,
       and_10_out, and_11_out, and_12_out, and_13_out, and_14_out, and_15_out, and_16_out, comparator_1_eq,
       comparator_2_eq, comparator_3_eq, comparator_4_eq, comparator_5_eq, comparator_6_eq, comparator_7_eq,
       comparator_8_eq, comparator_9_eq, comparator_10_eq, comparator_11_eq, comparator_12_eq,
       comparator_13_eq, comparator_14_eq, comparator_15_eq, comparator_16_eq, comparator_17_eq,
       comparator_18_eq, comparator_19_eq, comparator_20_eq, comparator_21_eq, comparator_22_eq,
       comparator_23_eq, comparator_24_eq, comparator_25_eq, comparator_26_eq, comparator_27_eq,
       comparator_28_eq, Is_Itype_out, or_1_out, or_3_out;
  wire [4:0] demultiplexer_1_out0, demultiplexer_2_out0, demultiplexer_2_out1, demultiplexer_3_out0,
       demultiplexer_3_out1, multiplexer_1_out;
  wire [15:0] bit_extender_1_out;

  Comparator #(.width(6)) comparator_1 (.a({6{1'b0}}), .b(Inst[31:26]), .eq(comparator_1_eq));  // open: gt, lt
  Comparator #(.width(6)) comparator_2 (.a(Inst[5:0]), .b(6'b100000), .eq(comparator_2_eq));  // open: gt, lt
  Comparator #(.width(6)) comparator_3 (.a(Inst[5:0]), .b(6'b100010), .eq(comparator_3_eq));  // open: gt, lt
  Comparator #(.width(6)) comparator_4 (.a(Inst[5:0]), .b(6'b011000), .eq(comparator_4_eq));  // open: gt, lt
  Comparator #(.width(6)) comparator_5 (.a(Inst[5:0]), .b(6'b011010), .eq(comparator_5_eq));  // open: gt, lt
  Comparator #(.width(6)) comparator_6 (.a(Inst[5:0]), .b(6'b010010), .eq(comparator_6_eq));  // open: gt, lt
  Comparator #(.width(6)) comparator_7 (.a(Inst[5:0]), .b(6'b010000), .eq(comparator_7_eq));  // open: gt, lt
  Comparator #(.width(6)) comparator_8 (.a(Inst[5:0]), .b({6{1'b0}}), .eq(comparator_8_eq));  // open: gt, lt
  Comparator #(.width(6)) comparator_9 (.a(Inst[5:0]), .b(6'b000010), .eq(comparator_9_eq));  // open: gt, lt
  Comparator #(.width(6)) comparator_10 (.a(Inst[5:0]), .b(6'b101010), .eq(comparator_10_eq));  // open: gt, lt
  Comparator #(.width(6)) comparator_11 (.a(Inst[5:0]), .b(6'b001000), .eq(comparator_11_eq));  // open: gt, lt
  Comparator #(.width(6)) comparator_12 (.a(Inst[5:0]), .b(6'b001001), .eq(comparator_12_eq));  // open: gt, lt
  Comparator #(.width(6)) comparator_13 (.a(Inst[5:0]), .b(6'b001100), .eq(comparator_13_eq));  // open: gt, lt
  Comparator #(.width(6)) comparator_14 (.a(Inst[5:0]), .b(6'b100100), .eq(comparator_14_eq));  // open: gt, lt
  Comparator #(.width(6)) comparator_15 (.a(Inst[5:0]), .b(6'b100101), .eq(comparator_15_eq));  // open: gt, lt
  Comparator #(.width(6)) comparator_16 (.a(Inst[5:0]), .b(6'b100111), .eq(comparator_16_eq));  // open: gt, lt
  Comparator #(.width(6)) comparator_17 (.a(Inst[5:0]), .b(6'b100110), .eq(comparator_17_eq));  // open: gt, lt
  Comparator #(.width(6)) comparator_18 (.a(Inst[31:26]), .b(6'b001000), .eq(comparator_18_eq));  // open: gt, lt
  Comparator #(.width(6)) comparator_19 (.a(Inst[31:26]), .b(6'b100011), .eq(comparator_19_eq));  // open: gt, lt
  Comparator #(.width(6)) comparator_20 (.a(Inst[31:26]), .b(6'b101011), .eq(comparator_20_eq));  // open: gt, lt
  Comparator #(.width(6)) comparator_21 (.a(Inst[31:26]), .b(6'b000100), .eq(comparator_21_eq));  // open: gt, lt
  Comparator #(.width(6)) comparator_22 (.a(Inst[31:26]), .b(6'b000101), .eq(comparator_22_eq));  // open: gt, lt
  Comparator #(.width(6)) comparator_23 (.a(Inst[31:26]), .b(6'b000010), .eq(comparator_23_eq));  // open: gt, lt
  Comparator #(.width(6)) comparator_24 (.a(Inst[31:26]), .b(6'b000011), .eq(comparator_24_eq));  // open: gt, lt
  Comparator #(.width(6)) comparator_25 (.a(Inst[31:26]), .b(6'b001100), .eq(comparator_25_eq));  // open: gt, lt
  Comparator #(.width(6)) comparator_26 (.a(Inst[31:26]), .b(6'b001101), .eq(comparator_26_eq));  // open: gt, lt
  Comparator #(.width(6)) comparator_27 (.a(Inst[31:26]), .b(6'b001110), .eq(comparator_27_eq));  // open: gt, lt
  Comparator #(.width(6)) comparator_28 (.a(Inst[31:26]), .b(6'b001111), .eq(comparator_28_eq));  // open: gt, lt
  Demultiplexer #(.width(5)) demultiplexer_1 (
    .out0(demultiplexer_1_out0), .out1(rt), .in(Inst[20:16]), .sel(comparator_1_eq));
  Demultiplexer #(.width(5)) demultiplexer_2 (
    .out0(demultiplexer_2_out0), .out1(demultiplexer_2_out1), .in(Inst[15:11]), .sel(comparator_1_eq));
  Demultiplexer #(.width(5)) demultiplexer_3 (
    .out0(demultiplexer_3_out0), .out1(demultiplexer_3_out1), .in(Inst[10:6]), .sel(comparator_1_eq));
  and and_1 (and_1_out, comparator_2_eq, comparator_1_eq);
  and and_2 (and_2_out, comparator_3_eq, comparator_1_eq);
  and and_3 (and_3_out, comparator_4_eq, comparator_1_eq);
  and and_4 (and_4_out, comparator_5_eq, comparator_1_eq);
  and and_5 (and_5_out, comparator_6_eq, comparator_1_eq);
  and and_6 (and_6_out, comparator_7_eq, comparator_1_eq);
  and and_7 (and_7_out, comparator_8_eq, comparator_1_eq);
  and and_8 (and_8_out, comparator_9_eq, comparator_1_eq);
  and and_9 (and_9_out, comparator_10_eq, comparator_1_eq);
  and and_10 (and_10_out, comparator_11_eq, comparator_1_eq);
  and and_11 (and_11_out, comparator_12_eq, comparator_1_eq);
  and and_12 (and_12_out, comparator_13_eq, comparator_1_eq);
  and and_13 (and_13_out, comparator_14_eq, comparator_1_eq);
  and and_14 (and_14_out, comparator_15_eq, comparator_1_eq);
  and and_15 (and_15_out, comparator_16_eq, comparator_1_eq);
  and and_16 (and_16_out, comparator_17_eq, comparator_1_eq);
  or or_1 (or_1_out, and_7_out, and_8_out);
  or Is_Itype (Is_Itype_out, comparator_18_eq, comparator_19_eq, comparator_20_eq, comparator_25_eq, comparator_26_eq, comparator_27_eq, comparator_28_eq);
  assign bit_extender_1_out = {{11{demultiplexer_3_out1[4]}}, demultiplexer_3_out1};  // Bit_Extender bit_extender_1
  Multiplexer #(.width(5)) multiplexer_1 (.in0(Inst[25:21]), .in1({5{1'b0}}), .out(multiplexer_1_out), .sel(or_1_out));
  Multiplexer #(.width(16)) multiplexer_2 (
    .in0(bit_extender_1_out), .in1({demultiplexer_2_out0, demultiplexer_3_out0, Inst[5:0]}), .out(imm),
    .sel(Is_Itype_out));
  Multiplexer #(.width(5)) multiplexer_3 (
    .in0(demultiplexer_1_out0), .in1(demultiplexer_2_out1), .out(rd), .sel(comparator_1_eq));
  or or_2 (imm_sel, Is_Itype_out, or_1_out);
  or or_3 (or_3_out, and_10_out, and_11_out, and_12_out);
  Multiplexer #(.width(5)) multiplexer_4 (.in0(multiplexer_1_out), .in1(rd), .out(rs), .sel(comparator_28_eq));
  nor nor_1 (reg_write_e, and_10_out, and_12_out);
  or or_4 (ALU_code[2], comparator_27_eq, and_16_out, and_9_out, and_7_out, and_8_out, and_5_out, and_6_out, comparator_28_eq);
  or or_5 (ALU_code[3], comparator_28_eq, comparator_26_eq, and_13_out, and_14_out, and_16_out, comparator_28_eq, and_15_out, and_9_out, or_3_out, comparator_25_eq, comparator_27_eq);
  or or_6 (ALU_code[0], and_2_out, and_4_out, and_6_out, and_8_out, and_13_out, comparator_25_eq, and_15_out, comparator_28_eq);
  or or_7 (ALU_code[1], and_14_out, and_8_out, and_7_out, and_3_out, and_4_out, and_15_out, comparator_26_eq);

  // Notes on the sheet:
  //   opcode for I and J type
  //   if 0 then it's R type
  //   funct code for R type
  //   R-type
  //   rd if r type
  //   last 6 bits of immediate if I type
  //   is_addi
  //   is_lw
  //   is_sw
  //   is_beq
  //   is_bne
  //   is_j
  //   is_jal
  //   andi
  //   ori
  //   xori
  //   lui
  //   rt if r type
  //   is_add
  //   is_sub
  //   is_mult
  //   is_div
  //   is_mflo
  //   is_mfhi
  //   is_sll
  //   is_slr
  //   is_slt
  //   is_jr
  //   is_jalr
  //   is_syscall
  //   is_and
  //   is_or
  //   is_nor
  //   is_xor
  //   shamt if not I type
  //   make 16 bit immediate/adrr
  //   this is 0 if sll or slr
  //   mux picks btn I type and shamt
  //   1 if either sll/slr or I type
  //   for LUI, make rd to rs
  //   Logic for ALU code
  //   is_jump
endmodule
