// Logisim project Proj2starter.circ as structural Verilog: 4 circuits, main circuit regfile
module CPUmain (
);

  wire control_1_imm_sel, control_1_reg_write_e;
  wire [3:0] control_1_alu_code;
  wire [4:0] control_1_rd, control_1_rs, control_1_rt;
  wire [31:0] alu_1_res, control_1_imm, multiplexer_1_out, regfile_1_rs_data, regfile_1_rt_data;

  regfile regfile_1 (
    .rt(control_1_rt), .rd(control_1_rd), .rd_data(alu_1_res), .write_e(control_1_reg_write_e),
    .rs(control_1_rs), .rs_data(regfile_1_rs_data), .rt_data(regfile_1_rt_data));
  Control control_1 (
    .rs(control_1_rs), .rt(control_1_rt), .rd(control_1_rd), .imm(control_1_imm),
    .reg_write_e(control_1_reg_write_e), .imm_sel(control_1_imm_sel), .ALU_code(control_1_alu_code));  // open: Inst
  Multiplexer #(.width(32)) multiplexer_1 (
    .in0(regfile_1_rt_data), .in1(control_1_imm), .out(multiplexer_1_out), .sel(control_1_imm_sel));
  ALU alu_1 (.OP1(regfile_1_rs_data), .OP2(multiplexer_1_out), .ALU_CODE(control_1_alu_code), .Res(alu_1_res[0]));
  regfile regfile_2 ();  // open: rt, rd, rd_data, write_e, rs, rs_data, rt_data
  Control control_2 ();  // open: Inst, rs, rt, rd, imm, reg_write_e, imm_sel, ALU_code
  ALU alu_2 ();  // open: OP1, OP2, ALU_CODE, Res
  // Pins of 1 and 32 bits meet at alu_1_res
endmodule

module regfile (
  input  [4:0] rs,
  input  [4:0] rt,
  input  [4:0] rd,
  input  write_e,
  input  [31:0] rd_data,
  output [31:0] rs_data,
  output [31:0] rt_data
);
endmodule

module ALU (
  input  [3:0] ALU_CODE,
  input  [31:0] OP1,
  input  [31:0] OP2,
  output Res
);

  Adder adder_1 ();  // open: a, b, out, cin, cout
  Subtractor subtractor_1 ();  // open: a, b, out, bin, bout
  Multiplier multiplier_1 ();  // open: a, b, out, cin, cout
  Divider divider_1 ();  // open: a, b, out, upper, rem
  Register HI ();  // open: D, en, clk, Q, clr
  Register LO ();  // open: D, en, clk, Q, clr
endmodule

module Control (
  input  [31:0] Inst,
  output [4:0] rs,
  output [4:0] rt,
  output [4:0] rd,
  output [31:0] imm,
  output reg_write_e,
  output imm_sel,
  output [3:0] ALU_code
);
endmodule
